// Logisim project Single-Cycle Datapath.circ as structural Verilog: 12 circuits, main circuit Datapath
module Datapath (
  input  in_1,
  output [1:0] ControlALUOp,
  output [1:0] ALUOp,
  output [31:0] PCNext,
  output [31:0] ALUOut
);

  wire and_1_out, clock_1_out, control_1_alusrc, control_1_branch, control_1_memread, control_1_memtoreg,
       control_1_memwrite, control_1_regdst, control_1_regwrite, n32_bit_alu_1_zero;
  wire [3:2] alu_control_1_operation;
  wire [4:0] multiplexer_1_out;
  wire [23:0] n32_to_24_bit_reducer_1_ouput, n32_to_24_bit_reducer_2_ouput;
  wire [31:0] adder_1_out, adder_2_out, bit_extender_1_out, multiplexer_2_out, n32_bit_alu_1_result,
       Program_Counter_q, ram_1_data, ram_2_data, register_file_1_read_data_1, register_file_1_read_data_2;

  Clock clock_1 (.out(clock_1_out));
  Register #(.width(32)) Program_Counter (.D(PCNext), .en(1'b1), .Q(Program_Counter_q), .clk(clock_1_out), .clr(in_1));
  _32_to_24_Bit_Reducer u_32_to_24_bit_reducer_1 (.Input(Program_Counter_q), .Ouput(n32_to_24_bit_reducer_1_ouput));
  Adder #(.width(32)) adder_1 (.a(Program_Counter_q), .b(32'h1), .out(adder_1_out), .cin(1'b0));  // open: cout
  RAM #(.addrWidth(24), .dataWidth(32)) ram_1 (
    .addr(n32_to_24_bit_reducer_1_ouput), .data(ram_1_data), .sel(1'b1), .clk(clock_1_out), .ld(1'b1),
    .clr(1'b0));
  Multiplexer #(.width(5), .enable("false")) multiplexer_1 (
    .in0(ram_1_data[20:16]), .in1(ram_1_data[15:11]), .out(multiplexer_1_out), .sel(control_1_regdst));
  Control control_1 (
    .OpCode(ram_1_data[31:26]), .RegDst(control_1_regdst), .Branch(control_1_branch),
    .MemRead(control_1_memread), .MemtoReg(control_1_memtoreg), .ALUOp(ControlALUOp),
    .MemWrite(control_1_memwrite), .ALUSrc(control_1_alusrc), .RegWrite(control_1_regwrite));
  assign bit_extender_1_out = {{16{ram_1_data[15]}}, ram_1_data[15:0]};  // Bit_Extender bit_extender_1
  Register_File register_file_1 (
    .Read_Register_1(ram_1_data[25:21]), .Read_Register_2(ram_1_data[20:16]),
    .Write_Register(multiplexer_1_out), .Write_Data(ALUOut), .RegWrite(control_1_regwrite),
    .Power(clock_1_out), .Read_Data_1(register_file_1_read_data_1), .Read_Data_2(register_file_1_read_data_2));
  Multiplexer #(.width(32), .enable("false")) multiplexer_2 (
    .in0(register_file_1_read_data_2), .in1(bit_extender_1_out), .out(multiplexer_2_out),
    .sel(control_1_alusrc));
  ALU_Control alu_control_1 (
    .ALUOp(ControlALUOp), .Function(ram_1_data[5:0]), .Operation({alu_control_1_operation, ALUOp}));
  _32_Bit_ALU u_32_bit_alu_1 (
    .A(register_file_1_read_data_1), .B(multiplexer_2_out), .Ainvert(alu_control_1_operation[3]),
    .Bnegate(alu_control_1_operation[2]), .Operation(ALUOp), .Result(n32_bit_alu_1_result),
    .Zero(n32_bit_alu_1_zero));  // open: CarryOut
  Adder #(.width(32)) adder_2 (.a(adder_1_out), .b(bit_extender_1_out), .out(adder_2_out), .cin(1'b0));  // open: cout
  _32_to_24_Bit_Reducer u_32_to_24_bit_reducer_2 (.Input(n32_bit_alu_1_result), .Ouput(n32_to_24_bit_reducer_2_ouput));
  Multiplexer #(.width(32), .enable("false")) multiplexer_3 (
    .in0(adder_1_out), .in1(adder_2_out), .out(PCNext), .sel(and_1_out));
  and and_1 (and_1_out, control_1_branch, n32_bit_alu_1_zero);
  RAM #(.addrWidth(24), .dataWidth(32), .bus("separate")) ram_2 (
    .addr(n32_to_24_bit_reducer_2_ouput), .din(register_file_1_read_data_2), .data(ram_2_data),
    .str(control_1_memwrite), .sel(1'b1), .clk(clock_1_out), .ld(control_1_memread), .clr(1'b0));
  Multiplexer #(.width(32), .enable("false")) multiplexer_4 (
    .in0(n32_bit_alu_1_result), .in1(ram_2_data), .out(ALUOut), .sel(control_1_memtoreg));

  // Notes on the sheet:
  //   Clock
  //   2 Clicks to Cycle
  //   Reset PC to Zero
  //   Instruction Memory
  //   1. Right-clicking -> Edit Contents...
  //   add  $3, $2, $1
  //   Programs can be loaded into Instruction Memory by:
  //   2. Selecting address space and typing in hexcode
  //   Example Program Statements:
  //   lw    $1, 0x0000
  //   lw    $2, 0x0001
  //   sw   $3, 0x0003
  //   lw    $1, 0x0002
  //   beq  $1, $3, 0x000a
  //   Logisim memory is aligned on 1-byte
  //   No shift needed
  //   ALU Control
  //   Data Memory
endmodule

// CarryOut
module _1_Bit_Adder___CarryOut (
  input  CarryIn,
  input  A,
  input  B,
  output CarryOut
);

  wire and_1_out, and_2_out, and_3_out;

  and and_1 (and_1_out, CarryIn, A);
  and and_2 (and_2_out, CarryIn, B);
  and and_3 (and_3_out, A, B);
  or or_1 (CarryOut, and_1_out, and_2_out, and_3_out);
endmodule

// Sum
module _1_Bit_Adder___Sum (
  input  CarryIn,
  input  A,
  input  B,
  output out_4
);

  wire and_1_out, and_2_out, and_3_out, and_4_out, not_1_out, not_2_out, not_3_out;

  not not_1 (not_1_out, A);
  not not_2 (not_2_out, B);
  not not_3 (not_3_out, CarryIn);
  and and_1 (and_1_out, A, not_2_out, not_3_out);
  and and_2 (and_2_out, not_1_out, B, not_3_out);
  and and_3 (and_3_out, not_1_out, not_2_out, CarryIn);
  and and_4 (and_4_out, A, B, CarryIn);
  or or_1 (out_4, and_1_out, and_2_out, and_3_out, and_4_out);
endmodule

// +
module _1_Bit_Adder (
  input  CarryIn,
  input  A,
  input  B,
  output Sum,
  output CarryOut
);

  _1_Bit_Adder___Sum u_1_bit_adder_sum_1 (.A(A), .B(B), .CarryIn(CarryIn), .out_4(Sum));
  _1_Bit_Adder___CarryOut u_1_bit_adder_carryout_1 (.A(A), .B(B), .CarryIn(CarryIn), .CarryOut(CarryOut));
endmodule

module _1_Bit_ALU (
  input  Ainvert,
  input  Binvert,
  input  CarryIn,
  input  [1:0] Operation,
  input  A,
  input  B,
  output Result,
  output CarryOut
);

  wire and_1_out, multiplexer_1_out, multiplexer_2_out, n1_bit_adder_1_sum, not_1_out, not_2_out, or_1_out;

  not not_1 (not_1_out, A);
  not not_2 (not_2_out, B);
  Multiplexer #(.enable("false")) multiplexer_1 (.in0(A), .in1(not_1_out), .out(multiplexer_1_out), .sel(Ainvert));
  Multiplexer #(.enable("false")) multiplexer_2 (.in0(B), .in1(not_2_out), .out(multiplexer_2_out), .sel(Binvert));
  and and_1 (and_1_out, multiplexer_1_out, multiplexer_2_out);
  or or_1 (or_1_out, multiplexer_1_out, multiplexer_2_out);
  _1_Bit_Adder u_1_bit_adder_1 (
    .A(multiplexer_1_out), .B(multiplexer_2_out), .CarryIn(CarryIn), .CarryOut(CarryOut),
    .Sum(n1_bit_adder_1_sum));
  Multiplexer #(.select(2), .enable("false")) multiplexer_3 (
    .in0(and_1_out), .in1(or_1_out), .in2(n1_bit_adder_1_sum), .out(Result), .sel(Operation));  // open: in3
endmodule

module _8_Bit_ALU (
  input  Ainvert,
  input  Binvert,
  input  CarryIn,
  input  [1:0] Operation,
  input  [7:0] A,
  input  [7:0] B,
  output [7:0] Result,
  output Zero,
  output CarryOut
);

  wire n1_bit_alu_1_carryout, n1_bit_alu_2_carryout, n1_bit_alu_3_carryout, n1_bit_alu_4_carryout,
       n1_bit_alu_5_carryout, n1_bit_alu_6_carryout, n1_bit_alu_7_carryout, or_1_out;

  _1_Bit_ALU u_1_bit_alu_1 (
    .A(A[0]), .B(B[0]), .Ainvert(Ainvert), .Binvert(Binvert), .CarryIn(CarryIn), .Operation(Operation),
    .CarryOut(n1_bit_alu_1_carryout), .Result(Result[0]));
  _1_Bit_ALU u_1_bit_alu_2 (
    .A(A[1]), .B(B[1]), .Ainvert(Ainvert), .Binvert(Binvert), .CarryIn(n1_bit_alu_1_carryout),
    .Operation(Operation), .CarryOut(n1_bit_alu_2_carryout), .Result(Result[1]));
  _1_Bit_ALU u_1_bit_alu_3 (
    .A(A[2]), .B(B[2]), .Ainvert(Ainvert), .Binvert(Binvert), .CarryIn(n1_bit_alu_2_carryout),
    .Operation(Operation), .CarryOut(n1_bit_alu_3_carryout), .Result(Result[2]));
  _1_Bit_ALU u_1_bit_alu_4 (
    .A(A[3]), .B(B[3]), .Ainvert(Ainvert), .Binvert(Binvert), .CarryIn(n1_bit_alu_3_carryout),
    .Operation(Operation), .CarryOut(n1_bit_alu_4_carryout), .Result(Result[3]));
  _1_Bit_ALU u_1_bit_alu_5 (
    .A(A[4]), .B(B[4]), .Ainvert(Ainvert), .Binvert(Binvert), .CarryIn(n1_bit_alu_4_carryout),
    .Operation(Operation), .CarryOut(n1_bit_alu_5_carryout), .Result(Result[4]));
  _1_Bit_ALU u_1_bit_alu_6 (
    .A(A[5]), .B(B[5]), .Ainvert(Ainvert), .Binvert(Binvert), .CarryIn(n1_bit_alu_5_carryout),
    .Operation(Operation), .CarryOut(n1_bit_alu_6_carryout), .Result(Result[5]));
  _1_Bit_ALU u_1_bit_alu_7 (
    .A(A[6]), .B(B[6]), .Ainvert(Ainvert), .Binvert(Binvert), .CarryIn(n1_bit_alu_6_carryout),
    .Operation(Operation), .CarryOut(n1_bit_alu_7_carryout), .Result(Result[6]));
  _1_Bit_ALU u_1_bit_alu_8 (
    .A(A[7]), .B(B[7]), .Ainvert(Ainvert), .Binvert(Binvert), .CarryIn(n1_bit_alu_7_carryout),
    .Operation(Operation), .CarryOut(CarryOut), .Result(Result[7]));
  not not_1 (Zero, or_1_out);
  or or_1 (or_1_out, Result[0], Result[1], Result[2], Result[3], Result[4], Result[5], Result[6], Result[7]);
endmodule

// ALU
module _32_Bit_ALU (
  input  Ainvert,
  input  Bnegate,
  input  [1:0] Operation,
  input  [31:0] A,
  input  [31:0] B,
  output [31:0] Result,
  output Zero,
  output CarryOut
);

  wire n8_bit_alu_1_carryout, n8_bit_alu_1_zero, n8_bit_alu_2_carryout, n8_bit_alu_2_zero,
       n8_bit_alu_3_carryout, n8_bit_alu_3_zero, n8_bit_alu_4_zero;

  _8_Bit_ALU u_8_bit_alu_1 (
    .A(A[7:0]), .B(B[7:0]), .Ainvert(Ainvert), .Binvert(Bnegate), .CarryIn(Bnegate), .Operation(Operation),
    .CarryOut(n8_bit_alu_1_carryout), .Result(Result[7:0]), .Zero(n8_bit_alu_1_zero));
  _8_Bit_ALU u_8_bit_alu_2 (
    .A(A[15:8]), .B(B[15:8]), .Ainvert(Ainvert), .Binvert(Bnegate), .CarryIn(n8_bit_alu_1_carryout),
    .Operation(Operation), .CarryOut(n8_bit_alu_2_carryout), .Result(Result[15:8]), .Zero(n8_bit_alu_2_zero));
  _8_Bit_ALU u_8_bit_alu_3 (
    .A(A[23:16]), .B(B[23:16]), .Ainvert(Ainvert), .Binvert(Bnegate), .CarryIn(n8_bit_alu_2_carryout),
    .Operation(Operation), .CarryOut(n8_bit_alu_3_carryout), .Result(Result[23:16]), .Zero(n8_bit_alu_3_zero));
  _8_Bit_ALU u_8_bit_alu_4 (
    .A(A[31:24]), .B(B[31:24]), .Ainvert(Ainvert), .Binvert(Bnegate), .CarryIn(n8_bit_alu_3_carryout),
    .Operation(Operation), .CarryOut(CarryOut), .Result(Result[31:24]), .Zero(n8_bit_alu_4_zero));
  and and_1 (Zero, n8_bit_alu_1_zero, n8_bit_alu_2_zero, n8_bit_alu_3_zero, n8_bit_alu_4_zero);
endmodule

module Control (
  input  [5:0] OpCode,
  output RegDst,
  output Branch,
  output MemRead,
  output MemtoReg,
  output [1:0] ALUOp,
  output MemWrite,
  output ALUSrc,
  output RegWrite
);

  wire not_1_out, not_2_out, not_3_out, not_4_out, not_5_out, not_6_out, not_7_out, not_8_out, not_9_out,
       not_10_out, not_11_out, not_12_out, not_13_out;

  not not_1 (not_1_out, OpCode[4]);
  not not_2 (not_2_out, OpCode[3]);
  not not_3 (not_3_out, OpCode[5]);
  not not_4 (not_4_out, OpCode[1]);
  not not_5 (not_5_out, OpCode[2]);
  and R_Type (ALUOp[1], not_3_out, not_1_out, not_2_out, not_5_out, not_4_out, not_6_out);
  not not_6 (not_6_out, OpCode[0]);
  not not_7 (not_7_out, OpCode[3]);
  not not_8 (not_8_out, OpCode[2]);
  and lw (MemRead, OpCode[5], not_1_out, not_7_out, not_8_out, OpCode[1], OpCode[0]);
  not not_9 (not_9_out, OpCode[2]);
  and sw (MemWrite, OpCode[5], not_1_out, OpCode[3], not_9_out, OpCode[1], OpCode[0]);
  not not_10 (not_10_out, OpCode[3]);
  not not_11 (not_11_out, OpCode[0]);
  not not_12 (not_12_out, OpCode[1]);
  not not_13 (not_13_out, OpCode[5]);
  and beq (ALUOp[0], not_13_out, not_1_out, not_10_out, OpCode[2], not_12_out, not_11_out);
  or or_1 (ALUSrc, MemRead, MemWrite);
  or or_2 (RegWrite, ALUOp[1], MemRead);

  assign Branch = ALUOp[0];
  assign MemtoReg = MemRead;
  assign RegDst = ALUOp[1];
endmodule

module ALU_Control (
  input  [1:0] ALUOp,
  input  [5:0] Function,
  output [3:0] Operation
);

  wire and_1_out, not_1_out, not_2_out, not_3_out, or_1_out;

  or or_1 (or_1_out, Function[3], Function[0]);
  and and_1 (and_1_out, ALUOp[1], Function[1]);
  and and_2 (Operation[0], ALUOp[1], or_1_out);
  not not_1 (not_1_out, ALUOp[0]);
  not not_2 (not_2_out, ALUOp[1]);
  not not_3 (not_3_out, Function[2]);
  and and_3 (Operation[3], ALUOp[0], not_1_out);
  or or_2 (Operation[2], ALUOp[0], and_1_out);
  or or_3 (Operation[1], not_2_out, not_3_out);
endmodule

// Reg
module Register_File (
  input  RegWrite,
  input  [4:0] Read_Register_1,
  input  [4:0] Read_Register_2,
  input  [4:0] Write_Register,
  input  [31:0] Write_Data,
  input  Power,
  output [31:0] Read_Data_1,
  output [31:0] Read_Data_2
);

  wire demultiplexer_1_out0, demultiplexer_1_out1, demultiplexer_1_out2, demultiplexer_1_out3,
       demultiplexer_1_out4, demultiplexer_1_out5, demultiplexer_1_out6, demultiplexer_1_out7,
       demultiplexer_1_out8, demultiplexer_1_out9, demultiplexer_1_out10, demultiplexer_1_out11,
       demultiplexer_1_out12, demultiplexer_1_out13, demultiplexer_1_out14, demultiplexer_1_out15;
  wire [31:0] _0_q, _1_q, _2_q, _3_q, _4_q, _5_q, _6_q, _7_q, _8_q, _9_q, _10_q, _11_q, _12_q, _13_q, _14_q,
       _15_q, demultiplexer_2_out0, demultiplexer_2_out1, demultiplexer_2_out2, demultiplexer_2_out3,
       demultiplexer_2_out4, demultiplexer_2_out5, demultiplexer_2_out6, demultiplexer_2_out7,
       demultiplexer_2_out8, demultiplexer_2_out9, demultiplexer_2_out10, demultiplexer_2_out11,
       demultiplexer_2_out12, demultiplexer_2_out13, demultiplexer_2_out14, demultiplexer_2_out15;

  Demultiplexer #(.select(5), .enable("false")) demultiplexer_1 (
    .out0(demultiplexer_1_out0), .out1(demultiplexer_1_out1), .out2(demultiplexer_1_out2),
    .out3(demultiplexer_1_out3), .out4(demultiplexer_1_out4), .out5(demultiplexer_1_out5),
    .out6(demultiplexer_1_out6), .out7(demultiplexer_1_out7), .out8(demultiplexer_1_out8),
    .out9(demultiplexer_1_out9), .out10(demultiplexer_1_out10), .out11(demultiplexer_1_out11),
    .out12(demultiplexer_1_out12), .out13(demultiplexer_1_out13), .out14(demultiplexer_1_out14),
    .out15(demultiplexer_1_out15), .in(RegWrite), .sel(Write_Register));  // open: out16, out17, out18, out19, out20, out21, out22, out23, out24, out25, out26, out27, out28, out29, out30, out31
  Demultiplexer #(.select(5), .width(32), .enable("false")) demultiplexer_2 (
    .out0(demultiplexer_2_out0), .out1(demultiplexer_2_out1), .out2(demultiplexer_2_out2),
    .out3(demultiplexer_2_out3), .out4(demultiplexer_2_out4), .out5(demultiplexer_2_out5),
    .out6(demultiplexer_2_out6), .out7(demultiplexer_2_out7), .out8(demultiplexer_2_out8),
    .out9(demultiplexer_2_out9), .out10(demultiplexer_2_out10), .out11(demultiplexer_2_out11),
    .out12(demultiplexer_2_out12), .out13(demultiplexer_2_out13), .out14(demultiplexer_2_out14),
    .out15(demultiplexer_2_out15), .in(Write_Data), .sel(Write_Register));  // open: out16, out17, out18, out19, out20, out21, out22, out23, out24, out25, out26, out27, out28, out29, out30, out31
  Register #(.width(32)) _0 (.D(demultiplexer_2_out0), .en(demultiplexer_1_out0), .Q(_0_q), .clk(Power));  // open: clr
  Register #(.width(32)) _4 (.D(demultiplexer_2_out4), .en(demultiplexer_1_out4), .Q(_4_q), .clk(Power));  // open: clr
  Register #(.width(32)) _8 (.D(demultiplexer_2_out8), .en(demultiplexer_1_out8), .Q(_8_q), .clk(Power));  // open: clr
  Register #(.width(32)) _12 (
    .D(demultiplexer_2_out12), .en(demultiplexer_1_out12), .Q(_12_q), .clk(Power));  // open: clr
  Register #(.width(32)) _1 (.D(demultiplexer_2_out1), .en(demultiplexer_1_out1), .Q(_1_q), .clk(Power));  // open: clr
  Register #(.width(32)) _5 (.D(demultiplexer_2_out5), .en(demultiplexer_1_out5), .Q(_5_q), .clk(Power));  // open: clr
  Register #(.width(32)) _9 (.D(demultiplexer_2_out9), .en(demultiplexer_1_out9), .Q(_9_q), .clk(Power));  // open: clr
  Register #(.width(32)) _13 (
    .D(demultiplexer_2_out13), .en(demultiplexer_1_out13), .Q(_13_q), .clk(Power));  // open: clr
  Register #(.width(32)) _2 (.D(demultiplexer_2_out2), .en(demultiplexer_1_out2), .Q(_2_q), .clk(Power));  // open: clr
  Register #(.width(32)) _6 (.D(demultiplexer_2_out6), .en(demultiplexer_1_out6), .Q(_6_q), .clk(Power));  // open: clr
  Register #(.width(32)) _10 (
    .D(demultiplexer_2_out10), .en(demultiplexer_1_out10), .Q(_10_q), .clk(Power));  // open: clr
  Register #(.width(32)) _14 (
    .D(demultiplexer_2_out14), .en(demultiplexer_1_out14), .Q(_14_q), .clk(Power));  // open: clr
  Register #(.width(32)) _3 (.D(demultiplexer_2_out3), .en(demultiplexer_1_out3), .Q(_3_q), .clk(Power));  // open: clr
  Register #(.width(32)) _7 (.D(demultiplexer_2_out7), .en(demultiplexer_1_out7), .Q(_7_q), .clk(Power));  // open: clr
  Register #(.width(32)) _11 (
    .D(demultiplexer_2_out11), .en(demultiplexer_1_out11), .Q(_11_q), .clk(Power));  // open: clr
  Register #(.width(32)) _15 (
    .D(demultiplexer_2_out15), .en(demultiplexer_1_out15), .Q(_15_q), .clk(Power));  // open: clr
  Multiplexer #(.select(5), .width(32), .enable("false")) multiplexer_1 (
    .in0(_0_q), .in1(_1_q), .in2(_2_q), .in3(_3_q), .in4(_4_q), .in5(_5_q), .in6(_6_q), .in7(_7_q),
    .in8(_8_q), .in9(_9_q), .in10(_10_q), .in11(_11_q), .in12(_12_q), .in13(_13_q), .in14(_14_q),
    .in15(_15_q), .out(Read_Data_1), .sel(Read_Register_1));  // open: in16, in17, in18, in19, in20, in21, in22, in23, in24, in25, in26, in27, in28, in29, in30, in31
  Multiplexer #(.select(5), .width(32), .enable("false")) multiplexer_2 (
    .in0(_0_q), .in1(_1_q), .in2(_2_q), .in3(_3_q), .in4(_4_q), .in5(_5_q), .in6(_6_q), .in7(_7_q),
    .in8(_8_q), .in9(_9_q), .in10(_10_q), .in11(_11_q), .in12(_12_q), .in13(_13_q), .in14(_14_q),
    .in15(_15_q), .out(Read_Data_2), .sel(Read_Register_2));  // open: in16, in17, in18, in19, in20, in21, in22, in23, in24, in25, in26, in27, in28, in29, in30, in31
endmodule

module _32_to_24_Bit_Reducer (
  input  [31:0] Input,
  output [23:0] Ouput
);


  assign Ouput = Input[23:0];
endmodule

// Shift
module _2_Bit_Shift (
  input  [31:0] Input,
  output [31:0] Output
);


  assign Output = {Input[29:0], 2'b00};
endmodule
